// Logisim project DE PROJECT FILE.circ as structural Verilog: 1 circuit, main circuit main
module main (
  input  [8:0] Fixed,
  input  [8:0] Fixed_2,
  input  [8:0] FIXED_3
);

  wire and_1_out, and_2_out, and_3_out, and_4_out, and_5_out, and_6_out, and_7_out, and_8_out, and_9_out,
       and_10_out, and_11_out, and_12_out, and_13_out, and_14_out, and_15_out, and_16_out, clock_1_out,
       clock_2_out, clock_3_out, clock_4_out, comparator_1_eq, counter_1_carry, counter_2_carry, Draw,
       not_1_out, or_10_out, or_23_out, p1, P1Win, p2, P2Win, p3, p4, p5, p6, p7, p8, p9, Turn, Valid_Turn;
  wire [8:0] multiplexer_1_out, multiplexer_2_out, multiplexer_4_out, multiplexer_5_out, or_1_out, or_12_out,
       or_13_out, or_24_out, Player1, Player1_prime, Player2, Player2_prime, register_2_q;

  or or_1 (or_1_out[0], p1, Player1[0]);
  or or_2 (or_1_out[1], p2, Player1[1]);
  or or_3 (or_1_out[2], p3, Player1[2]);
  or or_4 (or_1_out[3], p4, Player1[3]);
  or or_5 (or_1_out[4], p5, Player1[4]);
  or or_6 (or_1_out[5], p6, Player1[5]);
  or or_7 (or_1_out[6], p7, Player1[6]);
  or or_8 (or_1_out[7], p8, Player1[7]);
  or or_9 (or_1_out[8], p9, Player1[8]);
  Multiplexer #(.width(9)) multiplexer_1 (
    .in0(Player1), .in1(Player1_prime), .out(multiplexer_1_out), .sel(Valid_Turn));  // open: en
  and and_1 (and_1_out, Player1[8], Player1[7], Player1[6]);
  and and_2 (and_2_out, Player1[5], Player1[4], Player1[3]);
  and and_3 (and_3_out, Player1[2], Player1[1], Player1[0]);
  and and_4 (and_4_out, Player1[0], Player1[3], Player1[6]);
  and and_5 (and_5_out, Player1[1], Player1[4], Player1[7]);
  and and_6 (and_6_out, Player1[2], Player1[5], Player1[8]);
  and and_7 (and_7_out, Player1[0], Player1[4], Player1[8]);
  and and_8 (and_8_out, Player1[2], Player1[4], Player1[6]);
  Multiplexer #(.width(9)) multiplexer_2 (
    .in0(multiplexer_1_out), .in1(Fixed), .out(multiplexer_2_out), .sel(or_10_out));  // open: en
  or or_10 (or_10_out, P1Win, P2Win, Draw);
  or or_11 (P1Win, and_1_out, and_2_out, and_3_out, and_4_out, and_5_out, and_6_out, and_7_out, and_8_out);
  Multiplexer #(.width(9)) multiplexer_3 (
    .in0(Player1), .in1(or_1_out), .out(Player1_prime), .sel(not_1_out));  // open: en
  not not_1 (not_1_out, Turn);
  Register #(.width(9)) register_1 (.D(multiplexer_2_out), .Q(Player1), .clk(clock_1_out));  // open: en, clr
  Clock clock_1 (.out(clock_1_out));
  assign or_12_out = Player1_prime | Player2_prime;  // OR_Gate or_12, 9 bits wide
  Register #(.width(9)) register_2 (.D(or_12_out), .Q(register_2_q), .clk(clock_2_out));  // open: en, clr
  Clock clock_2 (.out(clock_2_out));
  LED led_1 (.in(Player1[0]));
  Button button_1 (.out(p1));
  LED led_2 (.in(Player1[3]));
  Button button_2 (.out(p4));
  Button button_3 (.out(p7));
  LED led_3 (.in(Player1[6]));
  Comparator #(.width(9)) comparator_1 (.a(or_12_out), .b(register_2_q), .eq(comparator_1_eq));  // open: gt, lt
  T_Flip_Flop t_ff_1 (.clk(clock_2_out), .T(Valid_Turn), .Q(Turn));  // open: Qn, preset, reset, en
  LED led_4 (.in(Player2[0]));
  Button button_4 (.out(p2));
  Button button_5 (.out(p5));
  LED led_5 (.in(Player2[3]));
  Button button_6 (.out(p8));
  LED led_6 (.in(Player2[6]));
  not not_2 (Valid_Turn, comparator_1_eq);
  LED led_7 (.in(Player1[1]));
  LED led_8 (.in(Player2[1]));
  LED led_9 (.in(Player2[4]));
  LED led_10 (.in(Player1[4]));
  LED led_11 (.in(Player1[7]));
  LED led_12 (.in(Player2[7]));
  or or_13 (or_13_out[0], p1, Player2[0]);
  or or_14 (or_13_out[1], p2, Player2[1]);
  or or_15 (or_13_out[2], p3, Player2[2]);
  or or_16 (or_13_out[3], p4, Player2[3]);
  or or_17 (or_13_out[4], p5, Player2[4]);
  or or_18 (or_13_out[5], p6, Player2[5]);
  or or_19 (or_13_out[6], p7, Player2[6]);
  or or_20 (or_13_out[7], p8, Player2[7]);
  or or_21 (or_13_out[8], p9, Player2[8]);
  Multiplexer #(.width(9)) multiplexer_4 (
    .in0(Player2), .in1(Player2_prime), .out(multiplexer_4_out), .sel(Valid_Turn));  // open: en
  LED led_13 (.in(Player1[2]));
  Button button_7 (.out(p3));
  LED led_14 (.in(Player2[2]));
  LED led_15 (.in(Player1[5]));
  Button button_8 (.out(p6));
  LED led_16 (.in(Player2[5]));
  Button button_9 (.out(p9));
  LED led_17 (.in(Player2[8]));
  LED led_18 (.in(Player1[8]));
  and and_9 (and_9_out, Player2[8], Player2[7], Player2[6]);
  and and_10 (and_10_out, Player2[5], Player2[4], Player2[3]);
  and and_11 (and_11_out, Player2[2], Player2[1], Player2[0]);
  and and_12 (and_12_out, Player2[0], Player2[3], Player2[6]);
  and and_13 (and_13_out, Player2[1], Player2[4], Player2[7]);
  and and_14 (and_14_out, Player2[2], Player2[5], Player2[8]);
  and and_15 (and_15_out, Player2[0], Player2[4], Player2[8]);
  and and_16 (and_16_out, Player2[2], Player2[4], Player2[6]);
  or or_22 (P2Win, and_9_out, and_10_out, and_11_out, and_12_out, and_13_out, and_14_out, and_15_out, and_16_out);
  or or_23 (or_23_out, P1Win, P2Win, Draw);
  Multiplexer #(.width(9)) multiplexer_5 (
    .in0(multiplexer_4_out), .in1(Fixed_2), .out(multiplexer_5_out), .sel(or_23_out));  // open: en
  Counter counter_1 (.count(P2Win), .carry(counter_1_carry), .clk(clock_4_out));  // open: load, D, Q, clr
  assign or_24_out = Player1 | Player2;  // OR_Gate or_24, 9 bits wide
  Multiplexer #(.width(9)) multiplexer_6 (.in0(Player2), .in1(or_13_out), .out(Player2_prime), .sel(Turn));  // open: en
  Register #(.width(9)) register_3 (.D(multiplexer_5_out), .Q(Player2), .clk(clock_3_out));  // open: en, clr
  Clock clock_3 (.out(clock_3_out));
  LED led_19 (.in(counter_1_carry));
  LED led_20 (.in(counter_2_carry));
  Counter counter_2 (.count(P1Win), .carry(counter_2_carry), .clk(clock_4_out));  // open: load, D, Q, clr
  Comparator #(.width(9)) comparator_2 (.a(or_24_out), .b(FIXED_3), .eq(Draw));  // open: gt, lt
  Clock clock_4 (.out(clock_4_out));
  LED led_21 (.in(Draw));

  // Other names for the same wires on the sheet: u1 = Player1[0]; u2 = Player1[1]; u3 = Player1[2]; u4 = Player1[3];
  //   u5 = Player1[4]; u6 = Player1[5]; u7 = Player1[6]; u8 = Player1[7]; u9 = Player1[8]; u1_prime = Player2[0];
  //   u2_prime = Player2[1]; u3_prime = Player2[2]; u4_prime = Player2[3]; u5_prime = Player2[4];
  //   u6_prime = Player2[5]; u7_prime = Player2[6]; u8_prime = Player2[7]; u9_prime = Player2[8]
endmodule
